# Fritzing sketch wiring (saved by Fritzing 0.9.3b)
breadboards: 1

parts:
  Soil3 = Adafruit STEMMA Soil Sensor - I2C Capacitive Moisture Sensor [part_number="I2C 0x38"]
  Soil2 = Adafruit STEMMA Soil Sensor - I2C Capacitive Moisture Sensor [part_number="I2C 0x37"]
  Soil1 = Adafruit STEMMA Soil Sensor - I2C Capacitive Moisture Sensor [part_number="I2C 0x36"]
  Waveshare_2_9in_ePaper_SPI = female pin header, 8 pins [form="♀ (female)"]
  BME680 = female pin header, 4 pins [form="♀ (female)"]
  Feather_M0_Lora = Adafruit Feather M0 RFM9x LoRa

nets:
  GND: Soil3.GND, Soil2.GND, Soil1.GND, Waveshare_2_9in_ePaper_SPI.pin7, BME680.pin1, Feather_M0_Lora.GND
  VIN: Soil3.VIN, Soil2.VIN, Soil1.VIN, Waveshare_2_9in_ePaper_SPI.pin8, BME680.pin4, Feather_M0_Lora.+3V3
  N1: Soil3.SDA, Soil2.SDA, Soil1.SDA, BME680.pin3, Feather_M0_Lora.SDA
  N2: Soil3.SCL, Soil2.SCL, Soil1.SCL, BME680.pin2, Feather_M0_Lora.SCL
  N3: Waveshare_2_9in_ePaper_SPI.pin1, Feather_M0_Lora.D10
  N4: Waveshare_2_9in_ePaper_SPI.pin2, Feather_M0_Lora.D9
  N5: Waveshare_2_9in_ePaper_SPI.pin3, Feather_M0_Lora.D6
  N6: Waveshare_2_9in_ePaper_SPI.pin4, Feather_M0_Lora.D5
  N7: Waveshare_2_9in_ePaper_SPI.pin5, Feather_M0_Lora.SCK
  N8: Waveshare_2_9in_ePaper_SPI.pin6, Feather_M0_Lora.MOSI

custom parts:
  Adafruit STEMMA Soil Sensor - I2C Capacitive Moisture Sensor: Most low cost soil sensors are resistive style, where there's two prongs and the sensor measures the conductivity between the two. These work OK at first, but eventually start to oxidize because of the exposed metal. Even if they're gold plated! The resistivity measurement goes up and up, so you constantly have to re-calibrate your code. Also, resistive measurements don't always work in loose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
  Adafruit Feather M0 RFM9x LoRa: This is the Adafruit Feather M0 RFM95 LoRa Radio - our take on an microcontroller with a "Long Range (LoRa)" packet radio transceiver with built in USB and battery charging. Its an Adafruit Feather M0 with a 433Mhz or 900MHz radio module cooked in! Great for making wireless networks that are more flexible than Bluetooth LE and without the high power requirements of WiFi. We have other boards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
